# Fritzing sketch ultrasound-sensor (saved by Fritzing 0.9.3b)
breadboards: 1

parts:
  hc-sr1 = hc-sr04
  Part1 = Arduino Uno (Rev3)

nets:
  VCC: hc-sr1.VCC, Part1.5V
  N1: hc-sr1.Trig, Part1.D13/SCK
  N2: hc-sr1.Echo, Part1.D12/MISO
  GND: hc-sr1.GND, Part1.GND

notes:
  Ultrasound Distance sensor to Arduino
  pin 12 = in
  pin 13 = out
